// Logisim project mips_single.circ as structural Verilog: 14 circuits, main circuit main
module main (
  input  in_1
);

  wire and_1_out, clock_1_out, comparator_1_eq, comparator_2_lt, comparator_3_lt, comparator_4_eq,
       control_unit_1_branch, control_unit_1_jump, control_unit_1_load_data, control_unit_1_lui,
       control_unit_1_mux_dest_operand_alu, control_unit_1_mux_jump, control_unit_1_mux_sa,
       control_unit_1_save_data, control_unit_1_unsign_compare, control_unit_1_use_register_address,
       control_unit_1_write_register, multiplexer_13_out, not_1_out;
  wire [3:0] control_unit_1_opcode_alu, control_unit_1_select_byte;
  wire [4:0] bit_extender_3_out, distribute_bitfields_1_rd, distribute_bitfields_1_rs,
       distribute_bitfields_1_rt, distribute_bitfields_1_sa, multiplexer_6_out, multiplexer_7_out,
       multiplexer_8_out, multiplexer_10_out;
  wire [5:0] distribute_bitfields_1_op_code, distribute_bitfields_1_out_11;
  wire [15:0] distribute_bitfields_1_out_6;
  wire [19:0] bit_extender_5_out;
  wire [25:0] distribute_bitfields_1_out_12;
  wire [31:0] adder_1_out, adder_2_out, adder_3_out, adder_4_out, bit_extender_1_out, bit_extender_2_out,
       bit_extender_4_out, mips_alu_1_p5, mips_ram_1_p3, mips_ram_1_p9, mipsprogramrom_1_p2,
       multiplexer_1_out, multiplexer_3_out, multiplexer_4_out, multiplexer_5_out, multiplexer_9_out,
       multiplexer_11_out, multiplexer_12_out, pull_resistor_1_node, register_1_q, registerfile_1_p8,
       shifter_1_out, shifter_2_out;

  Pull_Resistor #(.pull(1)) pull_resistor_1 (.node(pull_resistor_1_node[0]));
  Multiplexer #(.width(32), .enable("false")) multiplexer_1 (
    .in0(pull_resistor_1_node), .in1({32{1'b0}}), .out(multiplexer_1_out), .sel(pull_resistor_1_node[0]));
  Register #(.width(32)) register_1 (.D(multiplexer_1_out), .en(1'b1), .clk(clock_1_out), .Q(register_1_q), .clr(in_1));
  Clock clock_1 (.out(clock_1_out));
  // Probe on distribute_bitfields_1_op_code
  not not_1 (not_1_out, clock_1_out);
  Adder #(.width(32)) adder_1 (.a(32'h4), .b(multiplexer_3_out), .out(adder_1_out));  // open: cin, cout
  // Probe on nothing
  // MIPSProgramROM mipsprogramrom_1: pin names not known; wires that end beside it: register_1_q, mipsprogramrom_1_p2
  Adder #(.width(32)) adder_2 (.a(adder_1_out), .b(register_1_q), .out(adder_2_out));  // open: cin, cout
  Multiplexer #(.width(32), .enable("false")) multiplexer_2 (
    .in0(adder_2_out), .in1(multiplexer_4_out), .out(pull_resistor_1_node), .sel(control_unit_1_jump));
  Multiplexer #(.width(32), .enable("false")) multiplexer_3 (
    .in0({32{1'b0}}), .in1(shifter_1_out), .out(multiplexer_3_out), .sel(and_1_out));
  Multiplexer #(.width(32), .enable("false")) multiplexer_4 (
    .in0(adder_3_out), .in1(shifter_2_out), .out(multiplexer_4_out), .sel(control_unit_1_mux_jump));
  distribute_bitfields distribute_bitfields_1 (
    .RT(distribute_bitfields_1_rt), .in_1(mipsprogramrom_1_p2), .op_code(distribute_bitfields_1_op_code),
    .out_6(distribute_bitfields_1_out_6), .SA(distribute_bitfields_1_sa),
    .out_11(distribute_bitfields_1_out_11), .RS(distribute_bitfields_1_rs),
    .out_12(distribute_bitfields_1_out_12), .RD(distribute_bitfields_1_rd));  // open: out_9, out_3, func, out_7
  assign bit_extender_1_out = {{16{1'b0}}, distribute_bitfields_1_out_6};  // Bit_Extender bit_extender_1
  Shifter #(.width(32)) shifter_1 (.in(bit_extender_1_out), .\dist (5'b00010), .out(shifter_1_out));
  assign bit_extender_2_out = {{6{distribute_bitfields_1_out_12[25]}}, distribute_bitfields_1_out_12};  // Bit_Extender bit_extender_2
  control_unit control_unit_1 (
    .write_register(control_unit_1_write_register), .opcode_fields(distribute_bitfields_1_op_code),
    .function_fields(distribute_bitfields_1_out_11), .opcode_alu(control_unit_1_opcode_alu),
    .mux_dest_operand_alu(control_unit_1_mux_dest_operand_alu), .load_data(control_unit_1_load_data),
    .save_data(control_unit_1_save_data), .use_register_address(control_unit_1_use_register_address),
    .select_byte(control_unit_1_select_byte), .mux_sa(control_unit_1_mux_sa), .jump(control_unit_1_jump),
    .mux_jump(control_unit_1_mux_jump), .branch(control_unit_1_branch), .LUI(control_unit_1_lui),
    .unsign_compare(control_unit_1_unsign_compare));
  Multiplexer #(.width(32), .enable("false")) multiplexer_5 (
    .in0(multiplexer_11_out), .in1(register_1_q), .out(multiplexer_5_out),
    .sel(control_unit_1_use_register_address));
  Shifter #(.width(32)) shifter_2 (.in(bit_extender_2_out), .\dist (5'b00010), .out(shifter_2_out));
  Multiplexer #(.width(5), .enable("false")) multiplexer_6 (
    .in0(distribute_bitfields_1_rd), .in1(distribute_bitfields_1_rt), .out(multiplexer_6_out),
    .sel(control_unit_1_mux_dest_operand_alu));
  Multiplexer #(.width(5), .enable("false")) multiplexer_7 (
    .in0(multiplexer_6_out), .in1({5{1'b1}}), .out(multiplexer_7_out),
    .sel(control_unit_1_use_register_address));
  // RegisterFile registerfile_1: pin names not known; wires that end beside it: multiplexer_5_out, not_1_out, {5{1'b1}}, control_unit_1_write_register, multiplexer_7_out, distribute_bitfields_1_rs, distribute_bitfields_1_rt, registerfile_1_p8
  Bit_Extender #(.in_width(32), .out_width(5)) bit_extender_3 (.in(registerfile_1_p8), .out(bit_extender_3_out));
  Multiplexer #(.width(5), .enable("false")) multiplexer_8 (
    .in0(bit_extender_3_out), .in1(distribute_bitfields_1_sa), .out(multiplexer_8_out),
    .sel(control_unit_1_mux_sa));
  Multiplexer #(.width(32), .enable("false")) multiplexer_9 (
    .in0(mips_ram_1_p3), .in1(bit_extender_1_out), .out(multiplexer_9_out),
    .sel(control_unit_1_mux_dest_operand_alu));
  Multiplexer #(.width(5), .enable("false")) multiplexer_10 (
    .in0(multiplexer_8_out), .in1(5'b10000), .out(multiplexer_10_out), .sel(control_unit_1_lui));
  Adder #(.width(32)) adder_3 (.a(32'h4), .b(registerfile_1_p8), .out(adder_3_out));  // open: cin, cout
  Multiplexer #(.width(32), .enable("false")) multiplexer_11 (
    .in0(multiplexer_12_out), .in1(mips_ram_1_p9), .out(multiplexer_11_out), .sel(control_unit_1_load_data));
  // Mips_ALU mips_alu_1: pin names not known; wires that end beside it: registerfile_1_p8, multiplexer_9_out, control_unit_1_opcode_alu, multiplexer_10_out, mips_alu_1_p5
  and and_1 (and_1_out, control_unit_1_branch, comparator_1_eq);
  Comparator #(.width(32)) comparator_1 (.a(32'h1), .b(multiplexer_12_out), .eq(comparator_1_eq));  // open: gt, lt
  Comparator #(.width(32)) comparator_2 (
    .a(registerfile_1_p8), .b(multiplexer_9_out), .lt(comparator_2_lt));  // open: gt, eq
  Comparator #(.width(32), .mode("unsigned")) comparator_3 (
    .a(registerfile_1_p8), .b(multiplexer_9_out), .lt(comparator_3_lt));  // open: gt, eq
  Adder #(.width(32)) adder_4 (.a(registerfile_1_p8), .b(bit_extender_1_out), .out(adder_4_out));  // open: cin, cout
  Multiplexer #(.width(32), .enable("false")) multiplexer_12 (
    .in0(mips_alu_1_p5), .in1(bit_extender_4_out), .out(multiplexer_12_out), .sel(comparator_4_eq));
  Multiplexer #(.enable("false")) multiplexer_13 (
    .in0(comparator_2_lt), .in1(comparator_3_lt), .out(multiplexer_13_out),
    .sel(control_unit_1_unsign_compare));
  assign bit_extender_4_out = {{31{1'b0}}, multiplexer_13_out};  // Bit_Extender bit_extender_4
  Bit_Extender #(.in_width(32), .out_width(20)) bit_extender_5 (.in(adder_4_out), .out(bit_extender_5_out));
  // MIPS_RAM mips_ram_1: pin names not known; wires that end beside it: bit_extender_1_out, bit_extender_5_out, mips_ram_1_p3, control_unit_1_save_data, control_unit_1_select_byte, not_1_out, adder_4_out, control_unit_1_load_data, mips_ram_1_p9, 4'b1111
  // Probe on nothing
  // Probe on mips_ram_1_p3
  Comparator #(.width(4)) comparator_4 (
    .a(4'b1111), .b(control_unit_1_opcode_alu), .eq(comparator_4_eq));  // open: gt, lt

  // Notes on the sheet:
  //   contents of mipsprogramrom_1 (hex, n*v repeats v):
  //   # AUTHOR        :       Supasan Komonlit # ID           :       5910503871 # Date               :
  //   2019 , FEB 26  start_file: # label for first line       beq             $0 , $0 , init_program
  //   call_modulation:                        # We will collect first , second argument to t0 ,t1
  //   # show operate --> first % second       lw              $t0 , 0($sp)    lw              $t1 , 4($sp)
  //   addiu   $t2 , $0 , 1 start_loop_in_modulation:  slt             $t3 , $t0 , $t1 #  s0 < s1 ? s2 = 1
  //   , 0        beq             $t3 , $t2 , exit_loop_in_modulation     subu    $t0 , $t0 , $t1         j
  //   start_loop_in_modulation         exit_loop_in_modulation:       addu    $v1 , $t0 , $0          #
  //   move answer to $v0    jr              $ra  abort_r_hailstone:         lw              $fp , 0($sp)
  //   lw              $ra , 4($sp)    lw              $s0 , 8($sp)    addiu   $sp , $sp , 12  jr
  //   $ra  call_r_hailstone:                  # colelct first argument to s0  addiu   $t9 , $0 , 12   subu
  //   $sp , $sp , $t9 # We only reserve value for s0 , ra and old fp  sw              $s0 , 8($sp)    sw
  //   $ra , 4($sp)    sw              $fp , 0($sp)    addu    $fp , $sp , $0  lw              $s0 ,
  //   12($fp)   # load first argument to s0     addiu   $t0 , $0 , 1            bne             $s0 , $t0
  //   , condition_two_r_hailstone   addu    $v0 , $0 , $0   j               abort_r_hailstone
  //   condition_two_r_hailstone:     addiu   $t9 , $0 , 8    subu    $sp , $sp , $t9 # save argument for
  //   send to modulation  addiu   $t1 , $0 , 2    sw              $t1 , 4($sp)    sw              $s0 ,
  //   0($sp)    jal             call_modulation         addiu   $t9 , $0 , 8    addu    $sp , $sp , $t9
  //   bne             $v1 , $0 , last_case_hailstone  srl             $s0 , $s0 , 1   addiu   $t9 , $0 , 4
  //   subu    $sp , $sp , $t9         sw              $s0 , 0($sp)    jal             call_r_hailstone
  //   addiu   $t9 , $0 , 4    addu    $sp , $sp , $t9         addiu   $v0 , $v0 , 1   j
  //   abort_r_hailstone        last_case_hailstone:   addiu   $t9 , $0 , 4    subu    $sp , $sp , $t9
  //   sll             $s1 , $s0 , 1   addu    $s1 , $s1 , $s0         addiu   $s1 , $s1 , 1   sw
  //   $s1 , 0($sp)    jal             call_r_hailstone        addiu   $t9 , $0 , 4    addu    $sp , $sp ,
  //   $t9         addiu   $v0 , $v0 , 1   j               abort_r_hailstone                  init_program:
  //   # label for set program & reset value of register      addiu   $sp , $0 , 32767        addiu   $sp ,
  //   $sp , 32767       addiu   $sp , $sp , 2   addu    $ra , $0 , $0  main_program:    addiu   $t9 , $0 ,
  //   4    subu    $sp , $sp , $t9         addiu   $t6 , $0 , 5    sw              $t6 , 0($sp)    jal
  //   call_r_hailstone        addiu   $t9 , $0 , 4    addu    $sp , $sp , $t9         addu    $t7 , $v0 ,
  //   $0
endmodule

module distribute_bitfields (
  input  [31:0] in_1,
  output [4:0] SA,
  output [9:0] out_3,
  output [4:0] RD,
  output [4:0] RS,
  output [15:0] out_6,
  output [14:0] out_7,
  output [4:0] RT,
  output [9:0] out_9,
  output [19:0] func,
  output [5:0] out_11,
  output [25:0] out_12,
  output [5:0] op_code
);


  assign func = in_1[25:6];
  assign op_code = in_1[31:26];
  assign out_3 = in_1[15:6];
  assign out_6 = in_1[15:0];
  assign out_7 = in_1[20:6];
  assign out_9 = in_1[25:16];
  assign out_11 = in_1[5:0];
  assign out_12 = in_1[25:0];
  assign RD = in_1[15:11];
  assign RS = in_1[25:21];
  assign RT = in_1[20:16];
  assign SA = in_1[10:6];

  // Notes on the sheet:
  //   offset / imm
  //   target
  //   move from
  //   code / syscall
  //   REF : http://opencores.org/projects/plasma/opcodes
  //   multi / divide
  //   move to / jr
endmodule

module control_unit (
  input  [5:0] function_fields,
  input  [5:0] opcode_fields,
  output mux_sa,
  output unsign_compare,
  output [3:0] opcode_alu,
  output write_register,
  output jump,
  output mux_dest_operand_alu,
  output load_data,
  output save_data,
  output use_register_address,
  output [3:0] select_byte,
  output mux_jump,
  output branch,
  output LUI
);

  wire and_1_out, and_2_out, and_4_out, and_5_out, and_9_out, and_10_out, comparator_1_eq, not_1_out,
       not_2_out, not_3_out, not_4_out, not_5_out, not_6_out;

  not not_1 (not_1_out, opcode_fields[4]);
  not not_2 (not_2_out, opcode_fields[5]);
  not not_3 (not_3_out, opcode_fields[3]);
  Comparator #(.width(6)) comparator_1 (.a({6{1'b0}}), .b(opcode_fields), .eq(comparator_1_eq));  // open: gt, lt
  not not_4 (not_4_out, opcode_fields[2]);
  Multiplexer #(.enable("false")) multiplexer_1 (
    .in0(opcode_fields[0]), .in1(function_fields[0]), .out(unsign_compare), .sel(comparator_1_eq));
  not not_5 (not_5_out, opcode_fields[0]);
  not not_6 (not_6_out, opcode_fields[1]);
  and and_1 (and_1_out, opcode_fields[5], not_1_out, not_3_out, not_6_out, not_5_out);
  and and_2 (and_2_out, opcode_fields[5], not_1_out, not_3_out, not_4_out, opcode_fields[1], opcode_fields[0]);
  and and_3 (use_register_address, not_2_out, not_1_out, not_3_out, not_4_out, opcode_fields[1], opcode_fields[0]);
  and and_4 (and_4_out, not_4_out, opcode_fields[0]);
  and and_5 (and_5_out, not_6_out, opcode_fields[0]);
  and and_6 (mux_jump, not_1_out, not_3_out, not_2_out, not_4_out, opcode_fields[1]);
  and and_7 (branch, not_2_out, not_1_out, not_3_out, opcode_fields[2], not_6_out);
  and and_8 (LUI, not_2_out, not_1_out, opcode_fields[3], opcode_fields[2], opcode_fields[1], opcode_fields[0]);
  or or_1 (mux_dest_operand_alu, opcode_fields[5], opcode_fields[3], opcode_fields[1]);
  or or_2 (load_data, and_1_out, and_2_out);
  and and_9 (and_9_out, opcode_fields[5], not_1_out, opcode_fields[3], not_4_out, opcode_fields[1], opcode_fields[0]);
  and and_10 (and_10_out, opcode_fields[5], not_1_out, opcode_fields[3], not_4_out, not_6_out, not_5_out);
  or or_3 (select_byte[3], and_4_out, and_5_out);
  to_jump to_jump_1 (.function_bits(function_fields), .opcode_bits(opcode_fields), .out_3(jump));
  or or_4 (save_data, and_9_out, and_10_out);
  mux_sa_alu mux_sa_alu_1 (.func_bit_fields(function_fields), .mux_sa(mux_sa));
  to_opcode_alu to_opcode_alu_1 (.bit_function(function_fields), .bit_opcode(opcode_fields), .opcode_alu(opcode_alu));
  to_write_register to_write_register_1 (
    .function_fields(function_fields), .opcode_fields(opcode_fields), .write_register(write_register));

  assign select_byte[2:0] = {{2{select_byte[3]}}, opcode_fields[5]};

  // Notes on the sheet:
  //   A/5
  //   B/4
  //   C/3
  //   D/2
  //   E/1
  //   F/0
endmodule

module alu_case_function (
  input  [5:0] case_function,
  output [3:0] opcode_alu
);

  wire and_1_out, and_2_out, and_3_out, not_1_out, not_2_out, not_3_out, not_4_out, not_5_out, not_6_out;

  not not_1 (not_1_out, case_function[5]);
  not not_2 (not_2_out, case_function[4]);
  not not_3 (not_3_out, case_function[3]);
  not not_4 (not_4_out, case_function[2]);
  not not_5 (not_5_out, case_function[1]);
  not not_6 (not_6_out, case_function[0]);
  and and_1 (and_1_out, not_1_out, case_function[0]);
  and and_2 (and_2_out, case_function[5], case_function[0]);
  and and_3 (and_3_out, case_function[5], case_function[2]);
  or or_1 (opcode_alu[0], case_function[3], and_1_out);
  or or_2 (opcode_alu[1], case_function[3], and_2_out);
  or or_3 (opcode_alu[3], case_function[3], and_3_out);

  assign opcode_alu[2] = case_function[1];

  // Notes on the sheet:
  //   A/5
  //   C/3
  //   B/4
  //   D/2
  //   E/1
  //   F/0
endmodule

module alu_case_opcode (
  input  [5:0] case_opcode,
  output [3:0] opcode_alu
);

  wire and_1_out, and_2_out, and_3_out, not_1_out, not_2_out, not_3_out, not_4_out, not_5_out, not_6_out;
  wire [3:0] or_1_out;

  not not_1 (not_1_out, case_opcode[5]);
  not not_2 (not_2_out, case_opcode[4]);
  not not_3 (not_3_out, case_opcode[3]);
  not not_4 (not_4_out, case_opcode[2]);
  not not_5 (not_5_out, case_opcode[1]);
  not not_6 (not_6_out, case_opcode[0]);
  and and_1 (and_1_out, not_3_out, not_6_out);
  and and_2 (and_2_out, case_opcode[3], case_opcode[0]);
  and and_3 (and_3_out, not_1_out, not_2_out, case_opcode[3], case_opcode[2], case_opcode[1], case_opcode[0]);
  or or_1 (or_1_out[0], not_3_out, not_4_out);
  or or_2 (or_1_out[1], not_4_out, and_1_out, and_2_out);
  or or_3 (or_1_out[3], case_opcode[1], case_opcode[2]);
  Multiplexer #(.width(4), .enable("false")) multiplexer_1 (
    .in0({or_1_out[3], case_opcode[1], or_1_out[1:0]}), .in1(4'b0000), .out(opcode_alu), .sel(and_3_out));

  // Notes on the sheet:
  //   A/5
  //   C/3
  //   B/4
  //   D/2
  //   E/1
  //   F/0
endmodule

module to_opcode_alu (
  input  [5:0] bit_function,
  input  [5:0] bit_opcode,
  output [3:0] opcode_alu
);

  wire comparator_1_eq, not_1_out;
  wire [3:0] alu_case_function_1_opcode_alu, alu_case_opcode_1_opcode_alu;

  Comparator #(.width(6)) comparator_1 (.a(bit_opcode), .b({6{1'b0}}), .eq(comparator_1_eq));  // open: gt, lt
  not not_1 (not_1_out, comparator_1_eq);
  alu_case_function alu_case_function_1 (.case_function(bit_function), .opcode_alu(alu_case_function_1_opcode_alu));
  alu_case_opcode alu_case_opcode_1 (.case_opcode(bit_opcode), .opcode_alu(alu_case_opcode_1_opcode_alu));
  Multiplexer #(.width(4), .enable("false")) multiplexer_1 (
    .in0(alu_case_function_1_opcode_alu), .in1(alu_case_opcode_1_opcode_alu), .out(opcode_alu),
    .sel(not_1_out));
endmodule

module write_register_case_function (
  input  [5:0] func_bit_fields,
  output write_register
);

  wire not_1_out, not_2_out, not_3_out, not_4_out, not_5_out, not_6_out;

  not not_1 (not_1_out, func_bit_fields[4]);
  not not_2 (not_2_out, func_bit_fields[5]);
  not not_3 (not_3_out, func_bit_fields[3]);
  not not_4 (not_4_out, func_bit_fields[2]);
  not not_5 (not_5_out, func_bit_fields[0]);
  not not_6 (not_6_out, func_bit_fields[1]);
  or or_1 (write_register, not_3_out, func_bit_fields[1]);

  // Notes on the sheet:
  //   A/5
  //   B/4
  //   C/3
  //   E/1
  //   D/2
  //   F/0
endmodule

module standard_decision_op_code (
  input  [5:0] A_5,
  output [3:0] out_2
);

  wire not_1_out, not_2_out, not_3_out, not_4_out, not_5_out, not_6_out;

  not not_1 (not_1_out, A_5[5]);
  not not_2 (not_2_out, A_5[4]);
  not not_3 (not_3_out, A_5[3]);
  not not_4 (not_4_out, A_5[2]);
  not not_5 (not_5_out, A_5[0]);
  not not_6 (not_6_out, A_5[1]);

  // Notes on the sheet:
  //   B/4
  //   C/3
  //   D/2
  //   E/1
  //   F/0
endmodule

module write_register_case_opcode (
  input  [5:0] opode_bit_fields,
  output write_register
);

  wire and_1_out, and_2_out, and_3_out, not_1_out, not_2_out, not_3_out, not_4_out, not_5_out, not_6_out;

  not not_1 (not_1_out, opode_bit_fields[4]);
  not not_2 (not_2_out, opode_bit_fields[5]);
  not not_3 (not_3_out, opode_bit_fields[3]);
  not not_4 (not_4_out, opode_bit_fields[2]);
  not not_5 (not_5_out, opode_bit_fields[1]);
  not not_6 (not_6_out, opode_bit_fields[0]);
  and and_1 (and_1_out, not_2_out, opode_bit_fields[3]);
  and and_2 (and_2_out, opode_bit_fields[5], not_3_out);
  and and_3 (and_3_out, not_2_out, not_4_out, opode_bit_fields[0]);
  or or_1 (write_register, and_1_out, and_2_out, and_3_out);

  // Notes on the sheet:
  //   A/5
  //   B/4
  //   C/3
  //   E/1
  //   D/2
  //   F/0
endmodule

module to_write_register (
  input  [5:0] function_fields,
  input  [5:0] opcode_fields,
  output write_register
);

  wire comparator_1_eq, not_1_out, write_register_case_function_1_write_register,
       write_register_case_opcode_1_write_register;

  Comparator #(.width(6)) comparator_1 (.a(opcode_fields), .b({6{1'b0}}), .eq(comparator_1_eq));  // open: gt, lt
  not not_1 (not_1_out, comparator_1_eq);
  write_register_case_function write_register_case_function_1 (
    .func_bit_fields(function_fields), .write_register(write_register_case_function_1_write_register));
  write_register_case_opcode write_register_case_opcode_1 (
    .opode_bit_fields(opcode_fields), .write_register(write_register_case_opcode_1_write_register));
  Multiplexer #(.enable("false")) multiplexer_1 (
    .in0(write_register_case_function_1_write_register), .in1(write_register_case_opcode_1_write_register),
    .out(write_register), .sel(not_1_out));
endmodule

module mux_sa_alu (
  input  [5:0] func_bit_fields,
  output mux_sa
);

  wire not_1_out, not_2_out, not_3_out, not_5_out, not_6_out;

  not not_1 (not_1_out, func_bit_fields[4]);
  not not_2 (not_2_out, func_bit_fields[5]);
  not not_3 (not_3_out, func_bit_fields[3]);
  not not_4 (mux_sa, func_bit_fields[2]);
  not not_5 (not_5_out, func_bit_fields[0]);
  not not_6 (not_6_out, func_bit_fields[1]);

  // Notes on the sheet:
  //   A/5
  //   B/4
  //   C/3
  //   D/2
  //   E/1
  //   F/0
endmodule

module jump_case_function (
  input  [5:0] function_bitfields,
  output jump
);

  wire not_1_out, not_2_out, not_3_out, not_4_out, not_5_out, not_6_out;

  not not_1 (not_1_out, function_bitfields[4]);
  not not_2 (not_2_out, function_bitfields[5]);
  not not_3 (not_3_out, function_bitfields[3]);
  not not_4 (not_4_out, function_bitfields[2]);
  not not_5 (not_5_out, function_bitfields[1]);
  not not_6 (not_6_out, function_bitfields[0]);
  and and_1 (jump, not_2_out, not_1_out, function_bitfields[3], not_4_out, not_5_out, not_6_out);

  // Notes on the sheet:
  //   A/5
  //   B/4
  //   C/3
  //   E/1
  //   D/2
  //   F/0
endmodule

module jump_case_opcode (
  input  [5:0] opcode_bitfield,
  output jump
);

  wire not_1_out, not_2_out, not_3_out, not_4_out, not_5_out, not_6_out;

  not not_1 (not_1_out, opcode_bitfield[5]);
  not not_2 (not_2_out, opcode_bitfield[4]);
  not not_3 (not_3_out, opcode_bitfield[3]);
  not not_4 (not_4_out, opcode_bitfield[2]);
  not not_5 (not_5_out, opcode_bitfield[0]);
  not not_6 (not_6_out, opcode_bitfield[1]);
  and and_1 (jump, not_1_out, not_2_out, not_3_out, not_4_out, opcode_bitfield[1], opcode_bitfield[1]);

  // Notes on the sheet:
  //   A/5
  //   B/4
  //   C/3
  //   E/1
  //   D/2
  //   F/0
endmodule

module to_jump (
  input  [5:0] function_bits,
  input  [5:0] opcode_bits,
  output out_3
);

  wire comparator_1_eq, jump_case_function_1_jump, jump_case_opcode_1_jump, not_1_out;

  Comparator #(.width(6)) comparator_1 (.a(opcode_bits), .b({6{1'b0}}), .eq(comparator_1_eq));  // open: gt, lt
  not not_1 (not_1_out, comparator_1_eq);
  jump_case_function jump_case_function_1 (.function_bitfields(function_bits), .jump(jump_case_function_1_jump));
  jump_case_opcode jump_case_opcode_1 (.opcode_bitfield(opcode_bits), .jump(jump_case_opcode_1_jump));
  Multiplexer #(.enable("false")) multiplexer_1 (
    .in0(jump_case_function_1_jump), .in1(jump_case_opcode_1_jump), .out(out_3), .sel(not_1_out));
endmodule
