// Logisim project 5910503871_single_instruction.circ as structural Verilog: 8 circuits, main circuit main
module main (
  input  [31:0] in_1
);

  wire clock_1_out, control_unit_1_mux_dest_operand_alu, not_1_out, registerfile_1_p1, registerfile_1_p6;
  wire [3:0] to_opcode_alu_1_opcode_alu;
  wire [4:0] distribute_bitfields_1_rd, distribute_bitfields_1_rs, distribute_bitfields_1_rt,
       distribute_bitfields_1_sa, multiplexer_1_out;
  wire [5:0] distribute_bitfields_1_op_code, distribute_bitfields_1_out_11;
  wire [15:0] distribute_bitfields_1_out_6;
  wire [31:0] bit_extender_1_out, multiplexer_2_out, register_1_q, registerfile_1_p7;

  Register #(.width(32)) register_1 (.D(in_1), .en(1'b1), .clk(clock_1_out), .Q(register_1_q), .clr(1'b0));
  // MIPSProgramROM mipsprogramrom_1: pin names not known; wires that end beside it: register_1_q
  Clock clock_1 (.out(clock_1_out));
  not not_1 (not_1_out, clock_1_out);
  distribute_bitfields distribute_bitfields_1 (
    .RT(distribute_bitfields_1_rt), .out_6(distribute_bitfields_1_out_6), .RD(distribute_bitfields_1_rd),
    .SA(distribute_bitfields_1_sa), .op_code(distribute_bitfields_1_op_code),
    .out_11(distribute_bitfields_1_out_11), .RS(distribute_bitfields_1_rs));  // open: func, out_12, in_1, out_3, out_7, out_9
  control_unit control_unit_1 (
    .opcode(distribute_bitfields_1_op_code), .mux_dest_operand_alu(control_unit_1_mux_dest_operand_alu));
  Multiplexer #(.width(5), .enable("false")) multiplexer_1 (
    .in0(distribute_bitfields_1_rd), .in1(distribute_bitfields_1_rt), .out(multiplexer_1_out),
    .sel(control_unit_1_mux_dest_operand_alu));
  assign bit_extender_1_out = {{16{1'b0}}, distribute_bitfields_1_out_6};  // Bit_Extender bit_extender_1
  // RegisterFile registerfile_1: pin names not known; wires that end beside it: registerfile_1_p1, not_1_out, multiplexer_1_out, distribute_bitfields_1_rs, distribute_bitfields_1_rt, registerfile_1_p6, registerfile_1_p7
  Multiplexer #(.width(32), .enable("false")) multiplexer_2 (
    .in0(registerfile_1_p7), .in1(bit_extender_1_out), .out(multiplexer_2_out),
    .sel(control_unit_1_mux_dest_operand_alu));
  to_opcode_alu to_opcode_alu_1 (
    .bit_function(distribute_bitfields_1_out_11), .bit_opcode(distribute_bitfields_1_op_code),
    .opcode_alu(to_opcode_alu_1_opcode_alu));
  // Mips_ALU mips_alu_1: pin names not known; wires that end beside it: registerfile_1_p6, multiplexer_2_out, to_opcode_alu_1_opcode_alu, distribute_bitfields_1_sa, registerfile_1_p1

  // Notes on the sheet:
  //   contents of mipsprogramrom_1 (hex, n*v repeats v):
  //   addiu $s1, $zero, 2 addu $s2, $s0, $s1
endmodule

module distribute_bitfields (
  input  [31:0] in_1,
  output [4:0] SA,
  output [9:0] out_3,
  output [4:0] RD,
  output [4:0] RS,
  output [15:0] out_6,
  output [14:0] out_7,
  output [4:0] RT,
  output [9:0] out_9,
  output [19:0] func,
  output [5:0] out_11,
  output [25:0] out_12,
  output [5:0] op_code
);


  assign func = in_1[25:6];
  assign op_code = in_1[31:26];
  assign out_3 = in_1[15:6];
  assign out_6 = in_1[15:0];
  assign out_7 = in_1[20:6];
  assign out_9 = in_1[25:16];
  assign out_11 = in_1[5:0];
  assign out_12 = in_1[25:0];
  assign RD = in_1[15:11];
  assign RS = in_1[25:21];
  assign RT = in_1[20:16];
  assign SA = in_1[10:6];

  // Notes on the sheet:
  //   offset / imm
  //   target
  //   move from
  //   code / syscall
  //   REF : http://opencores.org/projects/plasma/opcodes
  //   multi / divide
  //   move to / jr
endmodule

module control_unit (
  input  [5:0] opcode,
  output mux_dest_operand_alu
);

  wire not_1_out, not_2_out, not_3_out, not_4_out, not_5_out, not_6_out;

  not not_1 (not_1_out, opcode[5]);
  not not_2 (not_2_out, opcode[4]);
  not not_3 (not_3_out, opcode[2]);
  not not_4 (not_4_out, opcode[3]);
  not not_5 (not_5_out, opcode[1]);
  not not_6 (not_6_out, opcode[0]);

  assign mux_dest_operand_alu = opcode[3];

  // Notes on the sheet:
  //   A/5
  //   C/3
  //   B/4
  //   D/2
  //   E/1
  //   F/0
endmodule

module alu_case_function (
  input  [5:0] case_function,
  output [3:0] opcode_alu
);

  wire and_1_out, and_2_out, and_3_out, not_1_out, not_2_out, not_3_out, not_4_out, not_5_out, not_6_out;

  not not_1 (not_1_out, case_function[5]);
  not not_2 (not_2_out, case_function[4]);
  not not_3 (not_3_out, case_function[3]);
  not not_4 (not_4_out, case_function[2]);
  not not_5 (not_5_out, case_function[1]);
  not not_6 (not_6_out, case_function[0]);
  and and_1 (and_1_out, not_1_out, case_function[0]);
  and and_2 (and_2_out, case_function[5], case_function[0]);
  and and_3 (and_3_out, case_function[5], case_function[2]);
  or or_1 (opcode_alu[0], case_function[3], and_1_out);
  or or_2 (opcode_alu[1], case_function[3], and_2_out);
  or or_3 (opcode_alu[3], case_function[3], and_3_out);

  assign opcode_alu[2] = case_function[1];

  // Notes on the sheet:
  //   A/5
  //   C/3
  //   B/4
  //   D/2
  //   E/1
  //   F/0
endmodule

module alu_case_opcode (
  input  [5:0] case_opcode,
  output [3:0] opcode_alu
);

  wire and_1_out, and_2_out, not_1_out, not_2_out, not_3_out, not_4_out, not_5_out, not_6_out;

  not not_1 (not_1_out, case_opcode[5]);
  not not_2 (not_2_out, case_opcode[4]);
  not not_3 (not_3_out, case_opcode[3]);
  not not_4 (not_4_out, case_opcode[2]);
  not not_5 (not_5_out, case_opcode[1]);
  not not_6 (not_6_out, case_opcode[0]);
  and and_1 (and_1_out, not_3_out, not_6_out);
  and and_2 (and_2_out, case_opcode[3], case_opcode[0]);
  or or_1 (opcode_alu[0], not_3_out, not_4_out);
  or or_2 (opcode_alu[1], not_4_out, and_1_out, and_2_out);
  or or_3 (opcode_alu[3], case_opcode[1], case_opcode[2]);

  assign opcode_alu[2] = case_opcode[1];

  // Notes on the sheet:
  //   A/5
  //   C/3
  //   B/4
  //   D/2
  //   E/1
  //   F/0
endmodule

module to_opcode_alu (
  input  [5:0] bit_function,
  input  [5:0] bit_opcode,
  output [3:0] opcode_alu
);

  wire comparator_1_eq, not_1_out;
  wire [3:0] alu_case_function_1_opcode_alu, alu_case_opcode_1_opcode_alu;

  Comparator #(.width(6)) comparator_1 (.a(bit_opcode), .b({6{1'b0}}), .eq(comparator_1_eq));  // open: gt, lt
  not not_1 (not_1_out, comparator_1_eq);
  alu_case_function alu_case_function_1 (.case_function(bit_function), .opcode_alu(alu_case_function_1_opcode_alu));
  alu_case_opcode alu_case_opcode_1 (.case_opcode(bit_opcode), .opcode_alu(alu_case_opcode_1_opcode_alu));
  Multiplexer #(.width(4), .enable("false")) multiplexer_1 (
    .in0(alu_case_function_1_opcode_alu), .in1(alu_case_opcode_1_opcode_alu), .out(opcode_alu),
    .sel(not_1_out));
endmodule

module write_register_case_function (
  input  [5:0] func_bit_fields,
  output write_register
);

  wire not_1_out, not_2_out, not_3_out, not_4_out, not_5_out, not_6_out;

  not not_1 (not_1_out, func_bit_fields[4]);
  not not_2 (not_2_out, func_bit_fields[5]);
  not not_3 (not_3_out, func_bit_fields[3]);
  not not_4 (not_4_out, func_bit_fields[2]);
  not not_5 (not_5_out, func_bit_fields[0]);
  not not_6 (not_6_out, func_bit_fields[1]);
  or or_1 (write_register, not_3_out, func_bit_fields[1]);

  // Notes on the sheet:
  //   A/5
  //   B/4
  //   C/3
  //   E/1
  //   D/2
  //   F/0
endmodule

module standard_decision_op_code (
  input  [5:0] A_5,
  output [3:0] out_2
);

  wire not_1_out, not_2_out, not_3_out, not_4_out, not_5_out, not_6_out;

  not not_1 (not_1_out, A_5[5]);
  not not_2 (not_2_out, A_5[4]);
  not not_3 (not_3_out, A_5[3]);
  not not_4 (not_4_out, A_5[2]);
  not not_5 (not_5_out, A_5[0]);
  not not_6 (not_6_out, A_5[1]);

  // Notes on the sheet:
  //   B/4
  //   C/3
  //   D/2
  //   E/1
  //   F/0
endmodule
