// Logisim project addiu.circ as structural Verilog: 2 circuits, main circuit main
module main (
  input  [31:0] in_1
);

  wire [31:0] mipsprogramrom_1_p2;

  // MIPSProgramROM mipsprogramrom_1: pin names not known; wires that end beside it: in_1, mipsprogramrom_1_p2
  control_unit control_unit_1 (.in_1(mipsprogramrom_1_p2));  // open: rs, rt, Immediate, rd, sham, func, Jump_target, Op_code
  // Mips_ALU mips_alu_1: pin names not known

  // Notes on the sheet:
  //   contents of mipsprogramrom_1 (hex, n*v repeats v):
  //   addiu $s1, $zero, 2 addu $s2, $s0, $s1
endmodule

module control_unit (
  input  [31:0] in_1,
  output [5:0] func,
  output [4:0] sham,
  output [4:0] rd,
  output [15:0] Immediate,
  output [4:0] rt,
  output [4:0] rs,
  output [25:0] Jump_target,
  output [5:0] Op_code
);


  assign func = in_1[5:0];
  assign Immediate = in_1[15:0];
  assign Jump_target = in_1[25:0];
  assign Op_code = in_1[31:26];
  assign rd = in_1[15:11];
  assign rs = in_1[20:16];
  assign rt = in_1[25:21];
  assign sham = in_1[10:6];
endmodule
