// Logisim project mips_single.circ as structural Verilog: 14 circuits, main circuit main
module main (
  input  in_1
);

  wire and_1_out, clock_1_out, comparator_1_eq, control_unit_1_branch, control_unit_1_jump,
       control_unit_1_load_data, control_unit_1_lui, control_unit_1_mux_dest_operand_alu,
       control_unit_1_mux_jump, control_unit_1_mux_sa, control_unit_1_save_data,
       control_unit_1_use_register_address, control_unit_1_write_register, not_1_out;
  wire [3:0] control_unit_1_opcode_alu, control_unit_1_select_byte;
  wire [4:0] distribute_bitfields_1_rd, distribute_bitfields_1_rs, distribute_bitfields_1_rt,
       distribute_bitfields_1_sa, multiplexer_6_out, multiplexer_7_out, multiplexer_8_out, multiplexer_10_out;
  wire [5:0] distribute_bitfields_1_op_code, distribute_bitfields_1_out_11;
  wire [15:0] distribute_bitfields_1_out_6;
  wire [19:0] bit_extender_3_out;
  wire [25:0] distribute_bitfields_1_out_12;
  wire [31:0] adder_1_out, adder_2_out, bit_extender_1_out, bit_extender_2_out, mips_alu_1_p5, mips_ram_1_p9,
       mipsprogramrom_1_p2, multiplexer_1_out, multiplexer_3_out, multiplexer_4_out, multiplexer_5_out,
       multiplexer_9_out, multiplexer_11_out, pull_resistor_1_node, register_1_q, registerfile_1_p8,
       registerfile_1_p9, shifter_1_out;

  Pull_Resistor #(.pull(1)) pull_resistor_1 (.node(pull_resistor_1_node[0]));
  Multiplexer #(.width(32), .enable("false")) multiplexer_1 (
    .in0(pull_resistor_1_node), .in1({32{1'b0}}), .out(multiplexer_1_out), .sel(pull_resistor_1_node[0]));
  Register #(.width(32)) register_1 (.D(multiplexer_1_out), .en(1'b1), .clk(clock_1_out), .Q(register_1_q), .clr(in_1));
  Clock clock_1 (.out(clock_1_out));
  not not_1 (not_1_out, clock_1_out);
  // MIPSProgramROM mipsprogramrom_1: pin names not known; wires that end beside it: register_1_q, mipsprogramrom_1_p2
  Adder #(.width(32)) adder_1 (.a(multiplexer_3_out), .b(register_1_q), .out(adder_1_out));  // open: cin, cout
  Multiplexer #(.width(32), .enable("false")) multiplexer_2 (
    .in0(adder_1_out), .in1(multiplexer_4_out), .out(pull_resistor_1_node), .sel(control_unit_1_jump));
  Multiplexer #(.width(32), .enable("false")) multiplexer_3 (
    .in0(32'h4), .in1(shifter_1_out), .out(multiplexer_3_out), .sel(and_1_out));
  Multiplexer #(.width(32), .enable("false")) multiplexer_4 (
    .in0(registerfile_1_p8), .in1(bit_extender_2_out), .out(multiplexer_4_out), .sel(control_unit_1_mux_jump));
  distribute_bitfields distribute_bitfields_1 (
    .RT(distribute_bitfields_1_rt), .RD(distribute_bitfields_1_rd), .out_12(distribute_bitfields_1_out_12),
    .in_1(mipsprogramrom_1_p2), .RS(distribute_bitfields_1_rs), .out_11(distribute_bitfields_1_out_11),
    .op_code(distribute_bitfields_1_op_code), .SA(distribute_bitfields_1_sa),
    .out_6(distribute_bitfields_1_out_6));  // open: out_9, out_7, out_3, func
  assign bit_extender_1_out = {{16{1'b0}}, distribute_bitfields_1_out_6};  // Bit_Extender bit_extender_1
  Shifter #(.width(32)) shifter_1 (.in(bit_extender_1_out), .\dist (5'b00010), .out(shifter_1_out));
  control_unit control_unit_1 (
    .mux_dest_operand_alu(control_unit_1_mux_dest_operand_alu),
    .write_register(control_unit_1_write_register), .opcode_alu(control_unit_1_opcode_alu),
    .opcode_fields(distribute_bitfields_1_op_code), .function_fields(distribute_bitfields_1_out_11),
    .load_data(control_unit_1_load_data), .save_data(control_unit_1_save_data),
    .use_register_address(control_unit_1_use_register_address), .select_byte(control_unit_1_select_byte),
    .mux_sa(control_unit_1_mux_sa), .jump(control_unit_1_jump), .mux_jump(control_unit_1_mux_jump),
    .branch(control_unit_1_branch), .LUI(control_unit_1_lui));
  Multiplexer #(.width(32), .enable("false")) multiplexer_5 (
    .in0(multiplexer_11_out), .in1(register_1_q), .out(multiplexer_5_out),
    .sel(control_unit_1_use_register_address));
  assign bit_extender_2_out = {{6{distribute_bitfields_1_out_12[25]}}, distribute_bitfields_1_out_12};  // Bit_Extender bit_extender_2
  Multiplexer #(.width(5), .enable("false")) multiplexer_6 (
    .in0(distribute_bitfields_1_rd), .in1(distribute_bitfields_1_rt), .out(multiplexer_6_out),
    .sel(control_unit_1_mux_dest_operand_alu));
  Multiplexer #(.width(5), .enable("false")) multiplexer_7 (
    .in0(multiplexer_6_out), .in1({5{1'b1}}), .out(multiplexer_7_out),
    .sel(control_unit_1_use_register_address));
  // RegisterFile registerfile_1: pin names not known; wires that end beside it: multiplexer_5_out, not_1_out, {5{1'b1}}, control_unit_1_write_register, multiplexer_7_out, distribute_bitfields_1_rs, distribute_bitfields_1_rt, registerfile_1_p8, registerfile_1_p9
  Multiplexer #(.width(5), .enable("false")) multiplexer_8 (
    .in0(distribute_bitfields_1_rs), .in1(distribute_bitfields_1_sa), .out(multiplexer_8_out),
    .sel(control_unit_1_mux_sa));
  Multiplexer #(.width(32), .enable("false")) multiplexer_9 (
    .in0(registerfile_1_p9), .in1(bit_extender_1_out), .out(multiplexer_9_out),
    .sel(control_unit_1_mux_dest_operand_alu));
  Multiplexer #(.width(5), .enable("false")) multiplexer_10 (
    .in0(multiplexer_8_out), .in1(5'b10000), .out(multiplexer_10_out), .sel(control_unit_1_lui));
  Multiplexer #(.width(32), .enable("false")) multiplexer_11 (
    .in0(mips_alu_1_p5), .in1(mips_ram_1_p9), .out(multiplexer_11_out), .sel(control_unit_1_load_data));
  // Mips_ALU mips_alu_1: pin names not known; wires that end beside it: registerfile_1_p8, multiplexer_9_out, control_unit_1_opcode_alu, multiplexer_10_out, mips_alu_1_p5
  and and_1 (and_1_out, control_unit_1_branch, comparator_1_eq);
  Comparator #(.width(32)) comparator_1 (.a(32'h1), .b(mips_alu_1_p5), .eq(comparator_1_eq));  // open: gt, lt
  // Probe on control_unit_1_opcode_alu
  Adder #(.width(32)) adder_2 (.a(registerfile_1_p8), .b(bit_extender_1_out), .out(adder_2_out));  // open: cin, cout
  Bit_Extender #(.in_width(32), .out_width(20)) bit_extender_3 (.in(adder_2_out), .out(bit_extender_3_out));
  // MIPS_RAM mips_ram_1: pin names not known; wires that end beside it: bit_extender_1_out, bit_extender_3_out, multiplexer_9_out, control_unit_1_save_data, control_unit_1_select_byte, not_1_out, adder_2_out, control_unit_1_load_data, mips_ram_1_p9

  // Notes on the sheet:
  //   contents of mipsprogramrom_1 (hex, n*v repeats v):
  //   # AUTHOR        :       Supasan Komonlit # Date         :       2019 , FEB 25  # First time for run
  //   file we will reset sp for reserve and ra start:     addiu   $sp , $0 , 32767        addiu   $sp ,
  //   $sp , 32767       addiu   $sp , $sp , 2 # Try to reserve array of int (fullword) 2^4 2^8 2^12 2^16 #
  //   label is first_array start at mem zero       addiu   $sp , $sp , -16         addiu   $t1 , $0 , 1
  //   sll             $t1 , $t1 , 4   sw              $t1 , 0($sp)    addiu   $t2 , $0 , 4    sllv    $t1
  //   , $t1 , $t2         sw              $t1 , 4($sp)    sllv    $t1 , $t1 , $t2         sw
  //   $t1 , 8($sp)    lui             $t1 , 1         sw              $t1 , 12($sp)   # When program close
  //   we will j for get pc to zero       j               start
endmodule

module distribute_bitfields (
  input  [31:0] in_1,
  output [4:0] SA,
  output [9:0] out_3,
  output [4:0] RD,
  output [4:0] RS,
  output [15:0] out_6,
  output [14:0] out_7,
  output [4:0] RT,
  output [9:0] out_9,
  output [19:0] func,
  output [5:0] out_11,
  output [25:0] out_12,
  output [5:0] op_code
);


  assign func = in_1[25:6];
  assign op_code = in_1[31:26];
  assign out_3 = in_1[15:6];
  assign out_6 = in_1[15:0];
  assign out_7 = in_1[20:6];
  assign out_9 = in_1[25:16];
  assign out_11 = in_1[5:0];
  assign out_12 = in_1[25:0];
  assign RD = in_1[15:11];
  assign RS = in_1[25:21];
  assign RT = in_1[20:16];
  assign SA = in_1[10:6];

  // Notes on the sheet:
  //   offset / imm
  //   target
  //   move from
  //   code / syscall
  //   REF : http://opencores.org/projects/plasma/opcodes
  //   multi / divide
  //   move to / jr
endmodule

module control_unit (
  input  [5:0] function_fields,
  input  [5:0] opcode_fields,
  output mux_sa,
  output [3:0] opcode_alu,
  output write_register,
  output jump,
  output mux_dest_operand_alu,
  output load_data,
  output save_data,
  output use_register_address,
  output [3:0] select_byte,
  output mux_jump,
  output branch,
  output LUI
);

  wire and_1_out, and_2_out, and_5_out, and_6_out, not_1_out, not_2_out, not_3_out, not_4_out, not_5_out,
       not_6_out;

  not not_1 (not_1_out, opcode_fields[4]);
  not not_2 (not_2_out, opcode_fields[5]);
  not not_3 (not_3_out, opcode_fields[3]);
  not not_4 (not_4_out, opcode_fields[2]);
  not not_5 (not_5_out, opcode_fields[0]);
  not not_6 (not_6_out, opcode_fields[1]);
  and and_1 (and_1_out, opcode_fields[5], not_1_out, not_3_out, not_6_out, not_5_out);
  and and_2 (and_2_out, opcode_fields[5], not_1_out, not_3_out, not_4_out, opcode_fields[1], opcode_fields[0]);
  and and_3 (save_data, opcode_fields[5], not_1_out, opcode_fields[3], not_4_out, opcode_fields[0]);
  and and_4 (use_register_address, not_2_out, not_1_out, not_3_out, not_4_out, opcode_fields[1], opcode_fields[0]);
  and and_5 (and_5_out, not_4_out, opcode_fields[0]);
  and and_6 (and_6_out, not_6_out, opcode_fields[0]);
  and and_7 (mux_jump, not_2_out, not_1_out, not_3_out, not_4_out, not_6_out, not_5_out);
  and and_8 (branch, not_2_out, not_1_out, not_3_out, opcode_fields[2], not_6_out);
  and and_9 (LUI, not_2_out, not_1_out, opcode_fields[3], opcode_fields[2], opcode_fields[1], opcode_fields[0]);
  and and_10 (mux_dest_operand_alu, opcode_fields[3], not_2_out);
  or or_1 (load_data, and_1_out, and_2_out);
  or or_2 (select_byte[3], and_5_out, and_6_out);
  to_jump to_jump_1 (.function_bits(function_fields), .opcode_bits(opcode_fields), .out_3(jump));
  mux_sa_alu mux_sa_alu_1 (.func_bit_fields(function_fields), .mux_sa(mux_sa));
  to_opcode_alu to_opcode_alu_1 (.bit_function(function_fields), .bit_opcode(opcode_fields), .opcode_alu(opcode_alu));
  to_write_register to_write_register_1 (
    .function_fields(function_fields), .opcode_fields(opcode_fields), .write_register(write_register));

  assign select_byte[2:0] = {{2{select_byte[3]}}, opcode_fields[5]};

  // Notes on the sheet:
  //   A/5
  //   B/4
  //   C/3
  //   D/2
  //   E/1
  //   F/0
endmodule

module alu_case_function (
  input  [5:0] case_function,
  output [3:0] opcode_alu
);

  wire and_1_out, and_2_out, and_3_out, and_4_out, not_1_out, not_2_out, not_3_out, not_4_out, not_5_out,
       not_6_out;
  wire [3:0] or_1_out;

  not not_1 (not_1_out, case_function[5]);
  not not_2 (not_2_out, case_function[4]);
  not not_3 (not_3_out, case_function[3]);
  not not_4 (not_4_out, case_function[2]);
  not not_5 (not_5_out, case_function[1]);
  not not_6 (not_6_out, case_function[0]);
  and and_1 (and_1_out, not_1_out, case_function[0]);
  and and_2 (and_2_out, case_function[5], case_function[0]);
  and and_3 (and_3_out, case_function[5], case_function[2]);
  and and_4 (and_4_out, not_1_out, not_2_out, case_function[3], case_function[2], case_function[1], case_function[0]);
  or or_1 (or_1_out[0], case_function[3], and_1_out);
  or or_2 (or_1_out[1], case_function[3], and_2_out);
  or or_3 (or_1_out[3], case_function[3], and_3_out);
  Multiplexer #(.width(4), .enable("false")) multiplexer_1 (
    .in0({or_1_out[3], case_function[1], or_1_out[1:0]}), .in1(4'b0000), .out(opcode_alu), .sel(and_4_out));

  // Notes on the sheet:
  //   A/5
  //   C/3
  //   B/4
  //   D/2
  //   E/1
  //   F/0
endmodule

module alu_case_opcode (
  input  [5:0] case_opcode,
  output [3:0] opcode_alu
);

  wire and_1_out, and_2_out, and_3_out, not_1_out, not_2_out, not_3_out, not_4_out, not_5_out, not_6_out;
  wire [3:0] or_1_out;

  not not_1 (not_1_out, case_opcode[5]);
  not not_2 (not_2_out, case_opcode[4]);
  not not_3 (not_3_out, case_opcode[3]);
  not not_4 (not_4_out, case_opcode[2]);
  not not_5 (not_5_out, case_opcode[1]);
  not not_6 (not_6_out, case_opcode[0]);
  and and_1 (and_1_out, not_3_out, not_6_out);
  and and_2 (and_2_out, case_opcode[3], case_opcode[0]);
  and and_3 (and_3_out, not_1_out, not_2_out, case_opcode[3], case_opcode[2], case_opcode[1], case_opcode[0]);
  or or_1 (or_1_out[0], not_3_out, not_4_out);
  or or_2 (or_1_out[1], not_4_out, and_1_out, and_2_out);
  or or_3 (or_1_out[3], case_opcode[1], case_opcode[2]);
  Multiplexer #(.width(4), .enable("false")) multiplexer_1 (
    .in0({or_1_out[3], case_opcode[1], or_1_out[1:0]}), .out(opcode_alu), .sel(and_3_out));  // open: in1

  // Notes on the sheet:
  //   A/5
  //   C/3
  //   B/4
  //   D/2
  //   E/1
  //   F/0
endmodule

module to_opcode_alu (
  input  [5:0] bit_function,
  input  [5:0] bit_opcode,
  output [3:0] opcode_alu
);

  wire comparator_1_eq, not_1_out;
  wire [3:0] alu_case_function_1_opcode_alu, alu_case_opcode_1_opcode_alu;

  Comparator #(.width(6)) comparator_1 (.a(bit_opcode), .b({6{1'b0}}), .eq(comparator_1_eq));  // open: gt, lt
  not not_1 (not_1_out, comparator_1_eq);
  alu_case_function alu_case_function_1 (.case_function(bit_function), .opcode_alu(alu_case_function_1_opcode_alu));
  alu_case_opcode alu_case_opcode_1 (.case_opcode(bit_opcode), .opcode_alu(alu_case_opcode_1_opcode_alu));
  Multiplexer #(.width(4), .enable("false")) multiplexer_1 (
    .in0(alu_case_function_1_opcode_alu), .in1(alu_case_opcode_1_opcode_alu), .out(opcode_alu),
    .sel(not_1_out));
endmodule

module write_register_case_function (
  input  [5:0] func_bit_fields,
  output write_register
);

  wire not_1_out, not_2_out, not_3_out, not_4_out, not_5_out, not_6_out;

  not not_1 (not_1_out, func_bit_fields[4]);
  not not_2 (not_2_out, func_bit_fields[5]);
  not not_3 (not_3_out, func_bit_fields[3]);
  not not_4 (not_4_out, func_bit_fields[2]);
  not not_5 (not_5_out, func_bit_fields[0]);
  not not_6 (not_6_out, func_bit_fields[1]);
  or or_1 (write_register, not_3_out, func_bit_fields[1]);

  // Notes on the sheet:
  //   A/5
  //   B/4
  //   C/3
  //   E/1
  //   D/2
  //   F/0
endmodule

module standard_decision_op_code (
  input  [5:0] A_5,
  output [3:0] out_2
);

  wire not_1_out, not_2_out, not_3_out, not_4_out, not_5_out, not_6_out;

  not not_1 (not_1_out, A_5[5]);
  not not_2 (not_2_out, A_5[4]);
  not not_3 (not_3_out, A_5[3]);
  not not_4 (not_4_out, A_5[2]);
  not not_5 (not_5_out, A_5[0]);
  not not_6 (not_6_out, A_5[1]);

  // Notes on the sheet:
  //   B/4
  //   C/3
  //   D/2
  //   E/1
  //   F/0
endmodule

module write_register_case_opcode (
  input  [5:0] opode_bit_fields,
  output write_register
);

  wire and_1_out, and_2_out, and_3_out, not_1_out, not_2_out, not_3_out, not_4_out, not_5_out, not_6_out;

  not not_1 (not_1_out, opode_bit_fields[4]);
  not not_2 (not_2_out, opode_bit_fields[5]);
  not not_3 (not_3_out, opode_bit_fields[3]);
  not not_4 (not_4_out, opode_bit_fields[2]);
  not not_5 (not_5_out, opode_bit_fields[1]);
  not not_6 (not_6_out, opode_bit_fields[0]);
  and and_1 (and_1_out, not_2_out, opode_bit_fields[3]);
  and and_2 (and_2_out, opode_bit_fields[5], not_3_out);
  and and_3 (and_3_out, not_2_out, not_4_out, opode_bit_fields[0]);
  or or_1 (write_register, and_1_out, and_2_out, and_3_out);

  // Notes on the sheet:
  //   A/5
  //   B/4
  //   C/3
  //   E/1
  //   D/2
  //   F/0
endmodule

module to_write_register (
  input  [5:0] function_fields,
  input  [5:0] opcode_fields,
  output write_register
);

  wire comparator_1_eq, not_1_out, write_register_case_function_1_write_register,
       write_register_case_opcode_1_write_register;

  Comparator #(.width(6)) comparator_1 (.a(opcode_fields), .b({6{1'b0}}), .eq(comparator_1_eq));  // open: gt, lt
  not not_1 (not_1_out, comparator_1_eq);
  write_register_case_function write_register_case_function_1 (
    .func_bit_fields(function_fields), .write_register(write_register_case_function_1_write_register));
  write_register_case_opcode write_register_case_opcode_1 (
    .opode_bit_fields(opcode_fields), .write_register(write_register_case_opcode_1_write_register));
  Multiplexer #(.enable("false")) multiplexer_1 (
    .in0(write_register_case_function_1_write_register), .in1(write_register_case_opcode_1_write_register),
    .out(write_register), .sel(not_1_out));
endmodule

module mux_sa_alu (
  input  [5:0] func_bit_fields,
  output mux_sa
);

  wire not_1_out, not_2_out, not_3_out, not_5_out, not_6_out;

  not not_1 (not_1_out, func_bit_fields[4]);
  not not_2 (not_2_out, func_bit_fields[5]);
  not not_3 (not_3_out, func_bit_fields[3]);
  not not_4 (mux_sa, func_bit_fields[2]);
  not not_5 (not_5_out, func_bit_fields[0]);
  not not_6 (not_6_out, func_bit_fields[1]);

  // Notes on the sheet:
  //   A/5
  //   B/4
  //   C/3
  //   D/2
  //   E/1
  //   F/0
endmodule

module jump_case_function (
  input  [5:0] function_bitfields,
  output jump
);

  wire not_1_out, not_2_out, not_3_out, not_4_out, not_5_out, not_6_out;

  not not_1 (not_1_out, function_bitfields[4]);
  not not_2 (not_2_out, function_bitfields[5]);
  not not_3 (not_3_out, function_bitfields[3]);
  not not_4 (not_4_out, function_bitfields[2]);
  not not_5 (not_5_out, function_bitfields[1]);
  not not_6 (not_6_out, function_bitfields[0]);
  and and_1 (jump, not_2_out, not_1_out, function_bitfields[3], not_4_out, not_5_out, not_6_out);

  // Notes on the sheet:
  //   A/5
  //   B/4
  //   C/3
  //   E/1
  //   D/2
  //   F/0
endmodule

module jump_case_opcode (
  input  [5:0] opcode_bitfield,
  output jump
);

  wire not_1_out, not_2_out, not_3_out, not_4_out, not_5_out, not_6_out;

  not not_1 (not_1_out, opcode_bitfield[5]);
  not not_2 (not_2_out, opcode_bitfield[4]);
  not not_3 (not_3_out, opcode_bitfield[3]);
  not not_4 (not_4_out, opcode_bitfield[2]);
  not not_5 (not_5_out, opcode_bitfield[0]);
  not not_6 (not_6_out, opcode_bitfield[1]);
  and and_1 (jump, not_1_out, not_2_out, not_3_out, not_4_out, opcode_bitfield[1], not_5_out);

  // Notes on the sheet:
  //   A/5
  //   B/4
  //   C/3
  //   E/1
  //   D/2
  //   F/0
endmodule

module to_jump (
  input  [5:0] function_bits,
  input  [5:0] opcode_bits,
  output out_3
);

  wire comparator_1_eq, jump_case_function_1_jump, jump_case_opcode_1_jump, not_1_out;

  Comparator #(.width(6)) comparator_1 (.a(opcode_bits), .b({6{1'b0}}), .eq(comparator_1_eq));  // open: gt, lt
  not not_1 (not_1_out, comparator_1_eq);
  jump_case_function jump_case_function_1 (.function_bitfields(function_bits), .jump(jump_case_function_1_jump));
  jump_case_opcode jump_case_opcode_1 (.opcode_bitfield(opcode_bits), .jump(jump_case_opcode_1_jump));
  Multiplexer #(.enable("false")) multiplexer_1 (
    .in0(jump_case_function_1_jump), .in1(jump_case_opcode_1_jump), .out(out_3), .sel(not_1_out));
endmodule
